# Fritzing sketch Alarm Clock (saved by Fritzing 0.9.3b)
breadboards: 1

parts:
  ZS-042_RTC1 = ZS-042 RTC Module
  U1 = Nokia 6100 Color LCD [package=nokia6100_lcd]
  Part2 = 24 NeoPixel Ring [part_number=1586]
  DFPlayer_Mini1 = DFPlayer MINI [package="DIP (Dual Inline) [THT]"]
  C1 = Electrolytic Capacitor [capacitance=0.1mF package="100 mil [THT, electrolytic]"]
  R1 = Resistor [tolerance=±5% resistance=1k package=THT]
  R2 = Resistor [tolerance=±5% resistance=1k package=THT]
  R3 = Photocell (LDR) [package=THT]
  R4 = Resistor [tolerance=±5% resistance=10k package=THT]
  Part4 = KY-015 Temperature & Humidity Sensor Module [package="Breakout board"]
  SP1 = SPEAKER [package=pcb_mount_speaker]
  Part5 = Arduino Mega 2560 (Rev3)

nets:
  GND: ZS-042_RTC1.GND, U1.VDIGITAL, U1.RESET, Part2.GND, DFPlayer_Mini1.GND#6, C1.-, Part5.GND
  VCC: ZS-042_RTC1.VCC, U1.CS, Part2.VDD, DFPlayer_Mini1.VCC, C1.+, Part4.Vin, Part5.5V
  N1: ZS-042_RTC1.SDA, Part5.D20/SDA
  N2: ZS-042_RTC1.SCL, Part5.D21/SCL
  N3: U1.DIO, Part5.D11_PWM
  N4: U1.SCK, Part5.D10_PWM
  N5: Part2.IN, Part5.D4_PWM
  N6: DFPlayer_Mini1.RX, R2.Pin_1
  N7: DFPlayer_Mini1.TX, R1.Pin_1
  N8: DFPlayer_Mini1.SPK1, SP1.-
  N9: DFPlayer_Mini1.SPK2, SP1.+
  N10: R1.Pin_0, Part5.D19/RX1
  N11: R2.Pin_0, Part5.D18/TX1
  N12: R3.pin_0, R4.Pin_1, Part5.A0
  N13: Part4.S, Part5.D3_PWM

notes:
  DS3231 RTC
  3.2" Basic Nextion Touch Display .
  4 Ohm 5W Speaker
  24 LED NeoPixel Ring
  100 uF Cap ( Optional )
  Power Input
  +5V GND

custom parts:
  24 NeoPixel Ring: 24 ultra bright smart LED NeoPixels are arranged in a circle with 2.6" (66mm) outer diameter. The rings are 'chainable' - connect the output pin of one to the input pin of another. Use only one microcontroller pin to control as many as you can chain together! Each LED is addressable as the driver chip is inside the LED. Each one has ~18mA constant current drive so the color will be very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
  DFPlayer MINI: MP3 module by DFRobot.com for playing Music from an SD-Card. Supports WAV and MP3 files.
  KY-015 Temperature & Humidity Sensor Module: KY-015 temperature and humidity sensor module, provides a low-latency serial interface to measure humidity and temperature.
