# Fritzing sketch Prototype Shield Layout (saved by Fritzing 0.9.3b)

parts:
  Part1 = Adafruit Proto Shield R3 [part_number="Adafruit #2077"]
  J1 = male pin header, 2 pins [form="♂ (male)"]
  J2 = male pin header, 4 pins [form="♂ (male)"]
  J3 = male pin header, 4 pins [form="♂ (male)"]
  J4 = Generic male header - 3 pins [form="♀ (female)" package=THT]
  J5 = Generic male header - 3 pins [form="♀ (female)" package=THT]
  J6 = Generic male header - 3 pins [form="♀ (female)" package=THT]
  J7 = male pin header, 2 pins [form="♂ (male)"]
  R1 = Resistor [tolerance=±5% resistance=1k package=THT]
  R2 = Resistor [tolerance=±5% resistance=1k package=THT]
  J8 = Generic male header - 3 pins [form="♀ (female)" package=THT]
  C1 = Electrolytic Capacitor [capacitance=1µF package="100 mil [THT, electrolytic]"]

nets:
  N1: Part1.GND, Part1.N$105, Part1.N$261, J2.pin4, J3.pin1, J4.Pin_2, J5.Pin_2, J6.Pin_3, J7.pin2, J8.Pin_2, C1.-
  N2: Part1.A0, Part1.1#117, Part1.P$5, J6.Pin_1
  N3: Part1.+5V, Part1.N$33, Part1.N$104, J2.pin3, J3.pin2, J4.Pin_1, J5.Pin_1, J6.Pin_2, J7.pin1, J8.Pin_1, C1.+
  N4: Part1.D3, Part1.N$173, J4.Pin_3
  N5: Part1.D4, Part1.N$138, J5.Pin_3
  N6: Part1.D10, Part1.N$69, J3.pin4
  N7: Part1.D11, Part1.N$14, J3.pin3
  N8: Part1.1#180, J8.Pin_3
  N9: Part1.N$18, Part1.N$43, J1.pin2, R2.Pin_0
  N10: Part1.N$19, Part1.N$80, J1.pin1, R1.Pin_0
  N11: Part1.N$83, Part1.N$103, J2.pin2, R2.Pin_1
  N12: Part1.N$84, Part1.N$113, J2.pin1, R1.Pin_1

custom parts:
  Adafruit Proto Shield R3: This prototyping shield is the best out there (well, we think so, at least), and now is even better with Version R3 - updated for the most compatibility with just about all the Arduinos! It works with UNO, Mega, Leonardo, NG, Diecimila, Duemilanove, and compatible Arduinos. Yun's and Arduino Ethernets have a chunky Ethernet jack that gets in the way of stacking, you can use the stacking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
  Generic male header - 3 pins: Generic male header
